// Logisim project Shelf-Secure-Circuit.circ as structural Verilog: 15 circuits, main circuit main
module main (
  input  M3,
  input  M4,
  output M0,
  output M1,
  output M2,
  output M3_2
);

  wire not_1_out, not_2_out;

  not not_1 (not_1_out, M3);
  not not_2 (not_2_out, M4);
  and and_1 (M0, not_2_out, not_1_out);
  and and_2 (M1, M4, not_1_out);
  and and_3 (M2, not_2_out, M3);
  and and_4 (M3_2, M4, M3);

  // Notes on the sheet:
  //   Shehyar Mallick
  //   S5328488
endmodule

module _2_to_4_decoder (
  input  M3,
  input  M4,
  output M0,
  output M1,
  output M2,
  output M3_2
);

  wire not_1_out, not_2_out;

  not not_1 (not_1_out, M3);
  not not_2 (not_2_out, M4);
  and and_1 (M0, not_2_out, not_1_out);
  and and_2 (M1, M4, not_1_out);
  and and_3 (M2, not_2_out, M3);
  and and_4 (M3_2, M4, M3);

  // Notes on the sheet:
  //   Shehryar Mallick
  //   S5328488
endmodule

module _3_to_8_decoder (
  input  M2,
  input  M3,
  input  M4,
  output M0,
  output M1,
  output M2_2,
  output M3_2,
  output M4_2,
  output M5,
  output M6,
  output M7
);

  wire n2_to_4_decoder_1_m0, n2_to_4_decoder_1_m1, n2_to_4_decoder_1_m2, n2_to_4_decoder_1_m3_2, not_1_out;

  not not_1 (not_1_out, M2);
  _2_to_4_decoder u_2_to_4_decoder_1 (
    .M0(n2_to_4_decoder_1_m0), .M1(n2_to_4_decoder_1_m1), .M2(n2_to_4_decoder_1_m2),
    .M3_2(n2_to_4_decoder_1_m3_2), .M3(M3), .M4(M4));
  and and_1 (M0, n2_to_4_decoder_1_m0, not_1_out);
  and and_2 (M1, n2_to_4_decoder_1_m1, not_1_out);
  and and_3 (M2_2, n2_to_4_decoder_1_m2, not_1_out);
  and and_4 (M3_2, n2_to_4_decoder_1_m3_2, not_1_out);
  and and_5 (M4_2, n2_to_4_decoder_1_m0, M2);
  and and_6 (M5, n2_to_4_decoder_1_m1, M2);
  and and_7 (M6, n2_to_4_decoder_1_m2, M2);
  and and_8 (M7, n2_to_4_decoder_1_m3_2, M2);

  // Notes on the sheet:
  //   Shehryar Mallick
  //   S5328488
endmodule

module _4_to_16_decoder (
  input  M1,
  input  M3,
  input  M2,
  input  M4,
  output out_5,
  output out_6,
  output out_7,
  output out_8,
  output out_9,
  output out_10,
  output out_11,
  output out_12,
  output out_13,
  output out_14,
  output out_15,
  output out_16,
  output out_17,
  output out_18,
  output out_19,
  output out_20
);

  wire n3_to_8_decoder_1_m0, n3_to_8_decoder_1_m1, n3_to_8_decoder_1_m2_2, n3_to_8_decoder_1_m3_2,
       n3_to_8_decoder_1_m4_2, n3_to_8_decoder_1_m5, n3_to_8_decoder_1_m6, n3_to_8_decoder_1_m7, not_1_out;

  not not_1 (not_1_out, M1);
  _3_to_8_decoder u_3_to_8_decoder_1 (
    .M0(n3_to_8_decoder_1_m0), .M1(n3_to_8_decoder_1_m1), .M2_2(n3_to_8_decoder_1_m2_2),
    .M3_2(n3_to_8_decoder_1_m3_2), .M4_2(n3_to_8_decoder_1_m4_2), .M5(n3_to_8_decoder_1_m5),
    .M6(n3_to_8_decoder_1_m6), .M7(n3_to_8_decoder_1_m7), .M2(M2), .M3(M3), .M4(M4));
  and and_1 (out_5, n3_to_8_decoder_1_m0, not_1_out);
  and and_2 (out_6, n3_to_8_decoder_1_m1, not_1_out);
  and and_3 (out_7, n3_to_8_decoder_1_m2_2, not_1_out);
  and and_4 (out_8, n3_to_8_decoder_1_m3_2, not_1_out);
  and and_5 (out_9, n3_to_8_decoder_1_m4_2, not_1_out);
  and and_6 (out_10, n3_to_8_decoder_1_m5, not_1_out);
  and and_7 (out_11, n3_to_8_decoder_1_m6, not_1_out);
  and and_8 (out_12, n3_to_8_decoder_1_m7, not_1_out);
  and and_9 (out_13, n3_to_8_decoder_1_m0, M1);
  and and_10 (out_14, n3_to_8_decoder_1_m1, M1);
  and and_11 (out_15, n3_to_8_decoder_1_m2_2, M1);
  and and_12 (out_16, n3_to_8_decoder_1_m3_2, M1);
  and and_13 (out_17, n3_to_8_decoder_1_m4_2, M1);
  and and_14 (out_18, n3_to_8_decoder_1_m5, M1);
  and and_15 (out_19, n3_to_8_decoder_1_m6, M1);
  and and_16 (out_20, n3_to_8_decoder_1_m7, M1);

  // Notes on the sheet:
  //   Shehryar Mallick
  //   S5328488
endmodule

module MAIN_CIRCUIT_PART_A (
  input  M1,
  input  M2,
  input  M3,
  input  M4,
  output January,
  output Odd_Months,
  output Even_Months,
  output December,
  output ERROR
);

  wire n4_to_16_decoder_1_out_6, n4_to_16_decoder_1_out_7, n4_to_16_decoder_1_out_8,
       n4_to_16_decoder_1_out_9, n4_to_16_decoder_1_out_10, n4_to_16_decoder_1_out_11,
       n4_to_16_decoder_1_out_12, n4_to_16_decoder_1_out_13, n4_to_16_decoder_1_out_14,
       n4_to_16_decoder_1_out_15, n4_to_16_decoder_1_out_17, n4_to_16_decoder_1_out_18,
       n4_to_16_decoder_1_out_19, n4_to_16_decoder_1_out_20;

  _4_to_16_decoder u_4_to_16_decoder_1 (
    .out_5(January), .out_6(n4_to_16_decoder_1_out_6), .out_7(n4_to_16_decoder_1_out_7),
    .out_8(n4_to_16_decoder_1_out_8), .out_9(n4_to_16_decoder_1_out_9), .out_10(n4_to_16_decoder_1_out_10),
    .out_11(n4_to_16_decoder_1_out_11), .out_12(n4_to_16_decoder_1_out_12),
    .out_13(n4_to_16_decoder_1_out_13), .out_14(n4_to_16_decoder_1_out_14),
    .out_15(n4_to_16_decoder_1_out_15), .out_16(December), .out_17(n4_to_16_decoder_1_out_17),
    .out_18(n4_to_16_decoder_1_out_18), .out_19(n4_to_16_decoder_1_out_19),
    .out_20(n4_to_16_decoder_1_out_20), .M1(M1), .M2(M2), .M3(M3), .M4(M4));
  _5_input_or_gate u_5_input_or_gate_1 (
    .IP1(n4_to_16_decoder_1_out_6), .IP2(n4_to_16_decoder_1_out_8), .IP3(n4_to_16_decoder_1_out_10),
    .IP4(n4_to_16_decoder_1_out_12), .IP5(n4_to_16_decoder_1_out_14), .OP(Odd_Months));
  _5_input_or_gate u_5_input_or_gate_2 (
    .IP1(n4_to_16_decoder_1_out_7), .IP2(n4_to_16_decoder_1_out_9), .IP3(n4_to_16_decoder_1_out_11),
    .IP4(n4_to_16_decoder_1_out_13), .IP5(n4_to_16_decoder_1_out_15), .OP(Even_Months));
  _4_input_or_gate u_4_input_or_gate_1 (
    .IP1(n4_to_16_decoder_1_out_17), .IP2(n4_to_16_decoder_1_out_18), .IP3(n4_to_16_decoder_1_out_19),
    .IP4(n4_to_16_decoder_1_out_20), .out_5(ERROR));

  // Notes on the sheet:
  //   Shehryar Mallick
  //   S5328488
endmodule

module _5_input_or_gate (
  input  IP1,
  input  IP2,
  input  IP3,
  input  IP4,
  input  IP5,
  output OP
);

  wire or_1_out, or_2_out, or_3_out;

  or or_1 (or_1_out, IP1, IP2);
  or or_2 (or_2_out, or_1_out, IP3);
  or or_3 (or_3_out, or_2_out, IP4);
  or or_4 (OP, or_3_out, IP5);

  // Notes on the sheet:
  //   Shehryar Mallick
  //   S5328488
endmodule

module _4_input_or_gate (
  input  IP1,
  input  IP2,
  input  IP3,
  input  IP4,
  output out_5
);

  wire or_1_out, or_2_out;

  or or_1 (or_1_out, IP1, IP2);
  or or_2 (or_2_out, or_1_out, IP3);
  or or_3 (out_5, or_2_out, IP4);

  // Notes on the sheet:
  //   Shehryar Mallick
  //   S5328488
endmodule

module _4_bit_full_adder_subtractor (
  input  SignBit,
  input  A3,
  input  B3,
  input  A2,
  input  B2,
  input  A1,
  input  B1,
  input  A0,
  input  B0,
  output COut,
  output S3,
  output S2,
  output S1,
  output S0
);

  wire n1_bit_full_adder_2_cout, n1_bit_full_adder_3_cout, n1_bit_full_adder_4_cout, xor_1_out, xor_2_out,
       xor_3_out, xor_4_out;

  xor xor_1 (xor_1_out, B3, SignBit);
  _1_bit_full_adder u_1_bit_full_adder_1 (.A(A3), .B(xor_1_out), .SUM(S3), .COut(COut), .Cin(n1_bit_full_adder_2_cout));
  xor xor_2 (xor_2_out, B2, SignBit);
  _1_bit_full_adder u_1_bit_full_adder_2 (
    .A(A2), .B(xor_2_out), .SUM(S2), .COut(n1_bit_full_adder_2_cout), .Cin(n1_bit_full_adder_3_cout));
  xor xor_3 (xor_3_out, B1, SignBit);
  _1_bit_full_adder u_1_bit_full_adder_3 (
    .A(A1), .B(xor_3_out), .SUM(S1), .COut(n1_bit_full_adder_3_cout), .Cin(n1_bit_full_adder_4_cout));
  xor xor_4 (xor_4_out, B0, SignBit);
  _1_bit_full_adder u_1_bit_full_adder_4 (
    .A(A0), .B(xor_4_out), .SUM(S0), .COut(n1_bit_full_adder_4_cout), .Cin(SignBit));

  // Notes on the sheet:
  //   Shehryar Mallick
  //   S5328488
endmodule

module _1_bit_full_adder (
  input  Cin,
  input  A,
  input  B,
  output SUM,
  output COut
);

  wire and_1_out, and_2_out, xor_1_out;

  xor xor_1 (xor_1_out, A, B);
  and and_1 (and_1_out, A, B);
  xor xor_2 (SUM, Cin, xor_1_out);
  and and_2 (and_2_out, Cin, xor_1_out);
  or or_1 (COut, and_2_out, and_1_out);

  // Notes on the sheet:
  //   Shehryar Mallick
  //   S5328488
endmodule

module MAIN_CIRCUIT_PART_B (
  input  in_1,
  input  in_2,
  input  in_3,
  input  in_4,
  output X1,
  output X0,
  output SB,
  output Q3,
  output Q2,
  output Q1,
  output Q0
);

  wire button_1_out, main_circuit_part_a_1_december, main_circuit_part_a_1_error,
       main_circuit_part_a_1_even_months, main_circuit_part_a_1_january, main_circuit_part_a_1_odd_months,
       n4_bit_full_adder_subtractor_1_s0, n4_bit_full_adder_subtractor_1_s1,
       n4_bit_full_adder_subtractor_1_s2, n4_bit_full_adder_subtractor_1_s3, not_1_out, not_2_out, not_3_out,
       not_4_out, not_5_out;

  MAIN_CIRCUIT_PART_A main_circuit_part_a_1 (
    .January(main_circuit_part_a_1_january), .Odd_Months(main_circuit_part_a_1_odd_months),
    .Even_Months(main_circuit_part_a_1_even_months), .December(main_circuit_part_a_1_december), .M1(in_1),
    .M2(in_2), .M3(in_3), .M4(in_4), .ERROR(main_circuit_part_a_1_error));
  not not_1 (not_1_out, main_circuit_part_a_1_error);
  not not_2 (not_2_out, main_circuit_part_a_1_december);
  not not_3 (not_3_out, main_circuit_part_a_1_even_months);
  not not_4 (not_4_out, main_circuit_part_a_1_odd_months);
  not not_5 (not_5_out, main_circuit_part_a_1_january);
  X1_Logic x1_logic_1 (
    .J(main_circuit_part_a_1_january), .D_prime(not_2_out), .J_prime(not_5_out),
    .D(main_circuit_part_a_1_december), .E_prime(not_3_out), .M_prime(not_4_out), .O_prime(not_1_out), .X1(X1));
  X0_Logic x0_logic_1 (
    .E(main_circuit_part_a_1_even_months), .D_prime(not_2_out), .E_prime(not_3_out),
    .D(main_circuit_part_a_1_december), .J_prime(not_5_out), .O_prime(not_4_out), .M_prime(not_1_out),
    .J_prime_2(not_5_out), .E_prime_2(not_3_out), .O(main_circuit_part_a_1_odd_months),
    .D_prime_2(not_2_out), .M_prime_2(not_1_out), .X0(X0));
  SB_Logic sb_logic_1 (
    .O(main_circuit_part_a_1_odd_months), .D_prime(not_2_out), .O_prime(not_4_out),
    .D(main_circuit_part_a_1_december), .J_prime(not_5_out), .E_prime(not_3_out), .M_prime(not_1_out), .SB(SB));
  _4_bit_full_adder_subtractor u_4_bit_full_adder_subtractor_1 (
    .SignBit(SB), .B3(1'b0), .B2(1'b0), .B1(X1), .B0(X0), .A3(Q3), .A2(Q2), .A1(Q1), .A0(Q0),
    .S0(n4_bit_full_adder_subtractor_1_s0), .S1(n4_bit_full_adder_subtractor_1_s1),
    .S3(n4_bit_full_adder_subtractor_1_s3), .S2(n4_bit_full_adder_subtractor_1_s2));  // open: COut
  Button button_1 (.out(button_1_out));
  _4_bit_D_Flipflop u_4_bit_d_flipflop_1 (
    .Clock(button_1_out), .D0(n4_bit_full_adder_subtractor_1_s0), .D1(n4_bit_full_adder_subtractor_1_s1),
    .D2(n4_bit_full_adder_subtractor_1_s2), .D3(n4_bit_full_adder_subtractor_1_s3), .Q0(Q0), .Q1(Q1),
    .Q2(Q2), .Q3(Q3));  // open: Q0_prime, Q1_prime, Q2_prime, Q3_prime

  // Notes on the sheet:
  //   Shehryar Mallick
  //   S5328488
endmodule

module _4_bit_D_Flipflop (
  input  Clock,
  input  D0,
  input  D1,
  input  D2,
  input  D3,
  output Q0,
  output Q0_prime,
  output Q1,
  output Q1_prime,
  output Q2,
  output Q2_prime,
  output Q3,
  output Q3_prime
);

  D_Flip_Flop d_ff_1 (.clk(Clock), .D(D0), .Q(Q0), .Qn(Q0_prime));  // open: preset, en, reset
  D_Flip_Flop d_ff_2 (.clk(Clock), .D(D1), .Q(Q1), .Qn(Q1_prime));  // open: preset, en, reset
  D_Flip_Flop d_ff_3 (.clk(Clock), .D(D2), .Q(Q2), .Qn(Q2_prime));  // open: preset, en, reset
  D_Flip_Flop d_ff_4 (.clk(Clock), .D(D3), .Q(Q3), .Qn(Q3_prime));  // open: preset, en, reset

  // Notes on the sheet:
  //   Shehryar Mallick
  //   S5328488
endmodule

module X1_Logic (
  input  J,
  input  D_prime,
  input  J_prime,
  input  D,
  input  E_prime,
  input  M_prime,
  input  O_prime,
  output X1
);

  wire and_1_out, and_2_out, and_3_out, and_4_out, or_1_out;

  and and_1 (and_1_out, J, D_prime);
  and and_2 (and_2_out, J_prime, D);
  and and_3 (and_3_out, M_prime, O_prime);
  or or_1 (or_1_out, and_1_out, and_2_out);
  and and_4 (and_4_out, E_prime, and_3_out);
  and and_5 (X1, or_1_out, and_4_out);

  // Notes on the sheet:
  //   Shehryar Mallick
  //   S5328488
endmodule

module X0_Logic (
  input  E,
  input  D_prime,
  input  E_prime,
  input  D,
  input  J_prime,
  input  O_prime,
  input  M_prime,
  input  J_prime_2,
  input  E_prime_2,
  input  O,
  input  D_prime_2,
  input  M_prime_2,
  output X0
);

  wire and_1_out, and_2_out, and_3_out, and_4_out, and_5_out, and_6_out, and_7_out, and_8_out, and_9_out,
       or_1_out;

  and and_1 (and_1_out, E, D_prime);
  and and_2 (and_2_out, E_prime, D);
  and and_3 (and_3_out, J_prime, O_prime);
  and and_4 (and_4_out, J_prime_2, E_prime_2);
  and and_5 (and_5_out, O, D_prime_2);
  or or_1 (or_1_out, and_1_out, and_2_out);
  and and_6 (and_6_out, and_3_out, M_prime);
  and and_7 (and_7_out, and_4_out, and_5_out);
  and and_8 (and_8_out, and_7_out, M_prime_2);
  and and_9 (and_9_out, or_1_out, and_6_out);
  or or_2 (X0, and_9_out, and_8_out);

  // Notes on the sheet:
  //   Shehryar Mallick
  //   S5328488
endmodule

module SB_Logic (
  input  O,
  input  D_prime,
  input  O_prime,
  input  D,
  input  J_prime,
  input  E_prime,
  input  M_prime,
  output SB
);

  wire and_1_out, and_2_out, and_3_out, and_4_out, or_1_out;

  and and_1 (and_1_out, O, D_prime);
  and and_2 (and_2_out, O_prime, D);
  and and_3 (and_3_out, J_prime, E_prime);
  or or_1 (or_1_out, and_1_out, and_2_out);
  and and_4 (and_4_out, and_3_out, M_prime);
  and and_5 (SB, or_1_out, and_4_out);

  // Notes on the sheet:
  //   Shehryar Mallick
  //   S5328488
endmodule

module testing (
);

  _2_to_4_decoder u_2_to_4_decoder_1 ();  // open: M0, M1, M2, M3_2, M3, M4
  _3_to_8_decoder u_3_to_8_decoder_1 ();  // open: M0, M1, M2_2, M3_2, M4_2, M5, M6, M7, M2, M3, M4
endmodule
